// Digital circuit D  flipflop.dig as structural Verilog
module D__flipflop (
  input  D,
  input  En,
  output Q,
  output Qn
);

  wire gated_d_latch_1_q, not_1_out;

  not not_1 (not_1_out, En);
  Gated_D_Latch gated_d_latch_1 (.D(D), .En(not_1_out), .Q(gated_d_latch_1_q));  // open: Qn
  Gated_D_Latch gated_d_latch_2 (.D(gated_d_latch_1_q), .En(En), .Q(Q), .Qn(Qn));
endmodule
